# Fritzing sketch StationMeteo (saved by Fritzing 0.9.4)
stripboards: 1

parts:
  WeMos_D1_Mini1 = WeMos D1 Mini
  I2c = male pin header, 4 pins [form="♂ (male)"]
  J3 = male pin header, 4 pins [form="♂ (male)"]
  H%_sol = JST-03JQ-BT [part_number=JST-JQ-BT package=THT]
  Pluviomètre = JST-03JQ-BT [part_number=JST-JQ-BT package=THT]
  Détecteur_pluie = JST-03JQ-BT [part_number=JST-JQ-BT package=THT]
  Anémomètre = JST-03JQ-BT [part_number=JST-JQ-BT package=THT]
  MOD-1016 = male pin header, 7 pins [form="♂ (male)"]
  R1 = Resistor [tolerance=±5% resistance=4.7k package=THT]
  Composant1 = Logic Level Converter
  1wire = JST-03JQ-BT [part_number=JST-JQ-BT package=THT]
  1wire2 = JST-03JQ-BT [part_number=JST-JQ-BT package=THT]
  Serial_3_3V = male pin header, 4 pins [form="♂ (male)"]

nets:
  N1: WeMos_D1_Mini1.3V3, I2c.pin1, J3.pin1, H%_sol.pin3, Détecteur_pluie.pin3, Anémomètre.pin3, R1.Pin_0, Composant1.LV, 1wire.pin3, 1wire2.pin3, Serial_3_3V.pin2
  N2: WeMos_D1_Mini1.5V, Pluviomètre.pin1, MOD-1016.pin7, Composant1.HV
  N3: WeMos_D1_Mini1.A0, H%_sol.pin1
  N4: WeMos_D1_Mini1.D1, I2c.pin4, J3.pin4, Composant1.TX2_LV
  N5: WeMos_D1_Mini1.D2, I2c.pin3, J3.pin3, Composant1.RX2_LV
  N6: WeMos_D1_Mini1.D3, R1.Pin_1, 1wire.pin1, 1wire2.pin1
  N7: WeMos_D1_Mini1.D4, Pluviomètre.pin3
  N8: WeMos_D1_Mini1.D5, MOD-1016.pin5
  N9: WeMos_D1_Mini1.D6, Détecteur_pluie.pin1
  N10: WeMos_D1_Mini1.D7, Anémomètre.pin1
  N11: WeMos_D1_Mini1.G, I2c.pin2, J3.pin2, H%_sol.pin2, Pluviomètre.pin2, Détecteur_pluie.pin2, Anémomètre.pin2, MOD-1016.pin1, Composant1.GND, 1wire.pin2, 1wire2.pin2, Serial_3_3V.pin1
  N12: WeMos_D1_Mini1.RX, Serial_3_3V.pin4
  N13: WeMos_D1_Mini1.TX, Serial_3_3V.pin3
  N14: MOD-1016.pin2, Composant1.RX2_HV
  N15: MOD-1016.pin4, Composant1.TX2_HV

custom parts:
  WeMos D1 Mini: The D1 mini is a mini wifi board based on ESP-8266EX.
