# Fritzing sketch StationMeteo2 (saved by Fritzing 0.9.4)
stripboards: 1

parts:
  WeMos_D1_Mini1 = WeMos D1 Mini
  Pluviomètre = JST-03JQ-BT [part_number=JST-JQ-BT package=THT]
  Anémomètre = JST-03JQ-BT [part_number=JST-JQ-BT package=THT]
  MOD-1016 = male pin header, 5 pins [form="♂ (male)"]
  Alim_5V = Screw terminal - 2 pins [package=THT]
  C1 = Electrolytic Capacitor [capacitance=0.47mF package="100 mil [THT, electrolytic]"]

nets:
  N1: WeMos_D1_Mini1.3V3, Anémomètre.pin1
  N2: WeMos_D1_Mini1.5V, Pluviomètre.pin1, MOD-1016.pin4, Alim_5V.pin2, C1.+
  N3: WeMos_D1_Mini1.D1, MOD-1016.pin2
  N4: WeMos_D1_Mini1.D2, MOD-1016.pin1
  N5: WeMos_D1_Mini1.D4, Pluviomètre.pin3
  N6: WeMos_D1_Mini1.D5, MOD-1016.pin3
  N7: WeMos_D1_Mini1.D7, Anémomètre.pin3
  N8: WeMos_D1_Mini1.G, Pluviomètre.pin2, Anémomètre.pin2, MOD-1016.pin5, Alim_5V.pin1, C1.-

custom parts:
  WeMos D1 Mini: The D1 mini is a mini wifi board based on ESP-8266EX.
